# Fritzing sketch te466_driver (saved by Fritzing 0.9.3b)
circuit board: 12.091cm x 8.78607cm
breadboards: 1

parts:
  Part1 = Monster Moto Shield
  M1 = DC Motor
  U1 = Voltage Regulator - 5V [package="TO220 [THT]"]
  Power_plug1 = Power plug
  S1 = Square Pushbutton
  S2 = Square Pushbutton
  Part3 = Arduino Nano (Rev3.0) (ICSP)
  Part4 = JeePlug experimenter's board

nets:
  N1: Part1.OUTA1, M1.pin_1
  N2: Part1.OUTB1, M1.pin_2
  VCC: Part1.VCC, U1.input_voltage, Power_plug1.VCC
  GND: Part1.GND, Part1.GND_-_GND@1, Part1.GND_-_GND@2, U1.GND, Power_plug1.GND, S1.leg0, S2.leg0, Part3.GND
  5V: Part1.5V, U1.output_voltage, Part3.5V, Part4.N$8, Part4.N$24
  N3: Part1.EN1_-_A0, Part3.D3, Part4.B3, Part4.A2
  N4: Part1.CS1_-_A2, Part3.A3, Part4.B1, Part4.A3
  N5: Part1.PWM1_-_D5, Part3.D9, Part4.B2, Part4.A6
  N6: Part1.INA1_-_D7, Part3.D5, Part4.B4, Part4.A4
  N7: Part1.INB1_-_D8, Part3.D6, Part4.B5, Part4.A5
  N8: S1.leg1, Part3.D7
  N9: S2.leg1, Part3.D8

notes:
  Minimum input voltage is 5.5V. Otherwise the VNH2SP30 chip will activate its low-voltage-shut-down.
  12V appears to be the intended application. 16V is the maximum.
  This Board is simply to re-arrange the pins from the SparkFun Monster Moto Shield to the way they're arranged on the TE466 knock-off board.

// code stored in the sketch: fritzing_code_copy.ino
/* 
 This code and the corresponding pin choices are intended for Arduino NANO v3.0
 
 Motor controller is a TE466 "mini" Monster Moto Shield.  
 Note: The TE466 is a MUCH cheaper (~$8) single-motor version of the dual-motor SparkFun Monster Moto Shield (~$70)
 
 Note: INA and INB control the direction (or braking) according to whether they're set HIGH or LOW.
    See details in the comments for the startMotor() function below.

 Note: This was adapted from the example code for the SparkFun (2-chip, 2-motor) Monster Moto Shield.
 Date: 2016/10/10
 Author: R Thomas
 
 Reminder: digitalWrite(analogPin, HIGH) turns on the built-in pull-up resistor for the pin
 Reminder: analogWrite(digitalPin, value) enables PWM output on the pin 
 */

#define STOP 0
#define BRAKEVCC 1
#define FORWARD   2
#define REVERSE  3
#define BRAKEGND 4
#define CS_THRESHOLD 100

/*  TE466 VNH2SP30 pin definitions */
// INA: digital/logic-level output HIGH for FORWARD, LOW for REVERSE
// direct connection to TE466 - INA
// Arduino NANO pin D5
static const uint8_t PIN_INA = 5;

// INB: digital/logic-level output LOW for FORWARD, HIGH for REVERSE
// direct connection to TE466 - INB
// Arduino NANO pin D6
static const uint8_t PIN_INB = 6;

// PWM: modulated digital/logic-level output to regulate duty-cycle on output
// direct connection to TE466 - PWM (sometimes labeled PMW)
// Arduino NANO pin D9
static const uint8_t PIN_PWM = 9;

// CS: analog input for "current sense"
// direct connection to TE466 - CS
// Arduino NANO pin A3
static const uint8_t PIN_CS = A3;

// EN: "ENable" status of switches output (Analog pin)
// direct connection to TE466 - EN
// Arduino NANO pin A6
static const uint8_t PIN_EN = A6;

// On board LED
static const uint8_t PIN_STATUS = 13;

static const uint8_t MAXIMUM_PROGRAM_STEPS = 100;

boolean motorCurrentFaultDetected = false;

class MotorState {
    uint8_t currentStateIna = LOW;
    uint8_t currentStateInb = LOW;
    uint8_t currentStatePwm = 0;
    uint8_t desiredStateIna = LOW;
    uint8_t desiredStateInb = LOW;
    uint8_t desiredStatePwm = 0;
    
  public:
    MotorState() {
      
    }
    
    void setDesiredState(uint8_t ina, uint8_t inb, uint8_t pwm) {
        desiredStateIna = ina;
        desiredStateInb = inb;
        desiredStatePwm = pwm;
    }
    
    void setMotorState() {
        if (desiredStateIna != currentStateIna) {
            currentStateIna = desiredStateIna;
            digitalWrite(PIN_INA, currentStateIna);
        }
        if (desiredStateInb != currentStateInb) {
            currentStateInb = desiredStateInb;
            digitalWrite(PIN_INB, currentStateInb);
        }
        if (desiredStatePwm != currentStatePwm) {
            currentStatePwm = desiredStatePwm;
            analogWrite(PIN_PWM, currentStatePwm);
        }
  }

};

class ProgramStep {
    long startTime = 0;
    uint8_t motorDirection = STOP;
    uint8_t motorSpeed = 0;
    long durationMillis = 0;
    
  public:
    ProgramStep(uint8_t motorDirection, uint8_t motorSpeed, long durationMillis) {
        this->motorDirection = motorDirection;
        this->motorSpeed = motorSpeed;
        this->durationMillis = durationMillis;
    }

    boolean activate(MotorState *motorState) {
        uint8_t newDesiredStateIna;
        uint8_t newDesiredStateInb;
        startTime = millis();
        if (motorDirection == FORWARD || motorDirection == BRAKEVCC)
            newDesiredStateIna = HIGH;
        else
            newDesiredStateIna= LOW;

        if ((motorDirection == BRAKEVCC) || (motorDirection == REVERSE))
            newDesiredStateInb = HIGH;
        else
            newDesiredStateInb = HIGH;
        
        motorState->setDesiredState(newDesiredStateIna, newDesiredStateInb, motorSpeed);
    }
    
    boolean isDurationComplete() {
        return (millis() > (startTime + durationMillis));
    }
    
};

class Program {
    uint8_t currentProgramStepIndex = 0;
    uint8_t programStepCount = 0;
    public:
        Program() {
        }
        
        ProgramStep *programSteps[MAXIMUM_PROGRAM_STEPS];
        
        void addProgramStep(ProgramStep *programStep) {
            // Check current programStepCount (1-based) against maximum
            if (programStepCount < MAXIMUM_PROGRAM_STEPS)  {
                programStepCount++;
                // array index is 0-based
                programSteps[programStepCount - 1] = programStep;
            }
        }
        
        ProgramStep getCurrentProgramStep() {
            if (programSteps[currentProgramStepIndex]->isDurationComplete()) {
                currentProgramStepIndex++;
                if (currentProgramStepIndex >= programStepCount) {
                    currentProgramStepIndex = 0;  // loop and repeat program
                }
            }
            return *programSteps[currentProgramStepIndex];
        }
};

MotorState *motor1State;

Program *currentProgram;

ProgramStep *activeProgramStep;

void setup()
{
    motor1State = new MotorState();
    currentProgram = new Program();
    
    // Serial.begin(9600); // TODO: Find out why this was here in the original sketch
  
    pinMode(PIN_STATUS, OUTPUT);

    // Init motor controller (digital and PWM) pins as outputs
    pinMode(PIN_INA, OUTPUT);
    pinMode(PIN_INB, OUTPUT);
    pinMode(PIN_PWM, OUTPUT);  // analogWrite will set PWM duty cycle

    // Init "enable" and "current sense" pins as inputs
    // TODO: Find out what exactly the EN pin does.  It is mapped to a connector on the motor shield board
    // but the example arduino code does nothing with the pin that is mapped/connected to it.
    pinMode(PIN_EN, INPUT);
    pinMode(PIN_CS, INPUT);

    // Initialize braked
    stopMotor();
    
    currentProgram->addProgramStep(new ProgramStep(FORWARD, 1023, 500));
    currentProgram->addProgramStep(new ProgramStep(REVERSE, 1023, 500));
    currentProgram->addProgramStep(new ProgramStep(REVERSE, 512, 2000));
    currentProgram->addProgramStep(new ProgramStep(REVERSE, 512, 2000));
}

void loop() {
    if (motorCurrentFaultDetected) {
        // fast-blink the on-board LED
        digitalWrite(PIN_STATUS, HIGH);
        delay(250);
        digitalWrite(PIN_STATUS, HIGH);
        delay(250);
    } else {
        // Check every loop to be sure the motor isn't stalled
        // or drawing too much current.
        if (analogRead(PIN_CS) < CS_THRESHOLD) {
            digitalWrite(PIN_STATUS, HIGH);
            // continue the program
            motor1State->setMotorState();
          
            ProgramStep currentProgramStepRef = currentProgram->getCurrentProgramStep();
            ProgramStep *currentProgramStep = &currentProgramStepRef;
            
            if (currentProgramStep != activeProgramStep) {
                activeProgramStep = currentProgramStep;
                currentProgramStep->activate(motor1State);
            }
        } else {
            stopMotor();
            motorCurrentFaultDetected = true;
        }
    }
    
}

void stopMotor() {
    digitalWrite(PIN_INA, LOW);
    digitalWrite(PIN_INB, LOW);
    analogWrite(PIN_PWM, 0);
}
